// Logisim project control-logic.circ as structural Verilog: 1 circuit, main circuit control_logic
module control_logic (
  input  [31:0] Instruction,
  input  BrEq,
  input  BrLt,
  output PCSel,
  output RegWEn,
  output [2:0] ImmSel,
  output BrUn,
  output ASel,
  output BSel,
  output [3:0] ALUSel,
  output MemWEn,
  output [1:0] WBSel
);

  wire and_1_out, and_2_out, and_3_out, and_4_out, and_5_out, and_6_out, and_7_out, and_9_out, and_10_out,
       and_11_out, and_12_out, and_13_out, and_14_out, and_15_out, and_16_out, and_17_out, and_18_out,
       and_19_out, and_20_out, and_21_out, and_22_out, and_23_out, and_24_out, and_25_out, and_26_out,
       and_27_out, and_28_out, and_29_out, and_30_out, and_31_out, and_32_out, and_33_out, and_34_out,
       and_35_out, and_36_out, and_37_out, and_38_out, and_39_out, and_40_out, and_41_out, and_42_out,
       and_43_out, B, comparator_18_eq, comparator_18_gt, comparator_18_lt, comparator_19_eq,
       comparator_19_gt, comparator_20_gt, comparator_20_lt, comparator_21_gt, comparator_21_lt, I1, I2, I3,
       InSel1, InSel2, InSel3, InSel4, InSel5, InSel6, InSel7, InSel8, InSel9, InSel10, InSel11, not_1_out,
       not_2_out, not_3_out, O30, O31, O32, O33, O34, O35, O36, O37, priority_encoder_1_out,
       priority_encoder_2_out, priority_encoder_3_out, priority_encoder_4_out, R1, S;
  wire [1:0] priority_encoder_5_out, priority_encoder_8_out, priority_encoder_9_out, priority_encoder_12_out;
  wire [2:0] priority_encoder_7_out;
  wire [3:0] priority_encoder_6_out, priority_encoder_10_out, priority_encoder_11_out,
       priority_encoder_13_out;
  wire [5:0] bit_extender_1_out, bit_extender_2_out, bit_extender_3_out, bit_extender_4_out,
       bit_extender_5_out, bit_extender_6_out, bit_extender_7_out, bit_extender_8_out, bit_extender_9_out,
       bit_extender_10_out, bit_extender_11_out, InsLabel, InsLabel1, InsLabel2, InsLabel3, InsLabel4,
       InsLabel5, InsLabel6, InsLabel7, InsLabel8, InsLabel9, InsLabel10, InsLabel11;
  wire [15:14] rom_1_data;

  // Probe on InsLabel
  ROM #(.addrWidth(6), .dataWidth(16)) rom_1 (
    .addr(InsLabel), .data({rom_1_data, WBSel, MemWEn, ALUSel, BSel, ASel, BrUn, ImmSel, RegWEn}));
  Comparator #(.mode("unsigned"), .width(7)) comparator_1 (
    .a(Instruction[6:0]), .b(7'b0110011), .eq(R1));  // open: gt, lt
  Comparator #(.mode("unsigned"), .width(7)) comparator_2 (
    .a(Instruction[6:0]), .b(7'b0000011), .eq(I1));  // open: gt, lt
  Comparator #(.mode("unsigned"), .width(7)) comparator_3 (
    .a(Instruction[6:0]), .b(7'b0010011), .eq(I2));  // open: gt, lt
  Comparator #(.mode("unsigned"), .width(7)) comparator_4 (
    .a(Instruction[6:0]), .b(7'b0100011), .eq(S));  // open: gt, lt
  Comparator #(.mode("unsigned"), .width(7)) comparator_5 (
    .a(Instruction[6:0]), .b(7'b1100011), .eq(B));  // open: gt, lt
  Comparator #(.mode("unsigned"), .width(7)) comparator_6 (
    .a(Instruction[6:0]), .b(7'b0010111), .eq(InSel8));  // open: gt, lt
  Comparator #(.mode("unsigned"), .width(7)) comparator_7 (
    .a(Instruction[6:0]), .b(7'b0110111), .eq(InSel9));  // open: gt, lt
  Comparator #(.mode("unsigned"), .width(7)) comparator_8 (
    .a(Instruction[6:0]), .b(7'b1101111), .eq(InSel10));  // open: gt, lt
  Comparator #(.mode("unsigned"), .width(7)) comparator_9 (
    .a(Instruction[6:0]), .b(7'b1100111), .eq(I3));  // open: gt, lt
  Comparator #(.mode("unsigned"), .width(3)) comparator_10 (
    .a(Instruction[14:12]), .b(3'b000), .eq(O30));  // open: gt, lt
  Comparator #(.mode("unsigned"), .width(3)) comparator_11 (
    .a(Instruction[14:12]), .b(3'b001), .eq(O31));  // open: gt, lt
  Comparator #(.mode("unsigned"), .width(3)) comparator_12 (
    .a(Instruction[14:12]), .b(3'b010), .eq(O32));  // open: gt, lt
  Comparator #(.mode("unsigned"), .width(3)) comparator_13 (
    .a(Instruction[14:12]), .b(3'b011), .eq(O33));  // open: gt, lt
  Comparator #(.mode("unsigned"), .width(3)) comparator_14 (
    .a(Instruction[14:12]), .b(3'b100), .eq(O34));  // open: gt, lt
  Comparator #(.mode("unsigned"), .width(3)) comparator_15 (
    .a(Instruction[14:12]), .b(3'b101), .eq(O35));  // open: gt, lt
  Comparator #(.mode("unsigned"), .width(3)) comparator_16 (
    .a(Instruction[14:12]), .b(3'b110), .eq(O36));  // open: gt, lt
  Comparator #(.mode("unsigned"), .width(3)) comparator_17 (
    .a(Instruction[14:12]), .b(3'b111), .eq(O37));  // open: gt, lt
  Comparator #(.mode("unsigned"), .width(7)) comparator_18 (
    .a(7'b0000001), .b(Instruction[31:25]), .gt(comparator_18_gt), .eq(comparator_18_eq),
    .lt(comparator_18_lt));
  and and_1 (and_1_out, and_9_out, comparator_19_gt);
  and and_2 (and_2_out, comparator_19_eq, and_9_out);
  and and_3 (and_3_out, O30, R1);
  and and_4 (and_4_out, I1, O30);
  and and_5 (and_5_out, I2, O30);
  and and_6 (and_6_out, S, O30);
  and and_7 (and_7_out, B, O30);
  and and_8 (InSel11, I3, O30);
  Comparator #(.mode("unsigned"), .width(7)) comparator_19 (
    .a(7'b0000001), .b(Instruction[31:25]), .gt(comparator_19_gt), .eq(comparator_19_eq));  // open: lt
  and and_9 (and_9_out, O31, R1);
  and and_10 (and_10_out, I1, O31);
  and and_11 (and_11_out, I2, O31);
  and and_12 (and_12_out, S, O31);
  and and_13 (and_13_out, B, O31);
  Priority_Encoder #(.select_enc(1)) priority_encoder_1 (
    .in0(InSel8), .out(priority_encoder_1_out));  // open: in1, gs, en_out, en_in
  Priority_Encoder #(.select_enc(1)) priority_encoder_2 (
    .in0(InSel9), .out(priority_encoder_2_out));  // open: in1, gs, en_out, en_in
  Priority_Encoder #(.select_enc(1)) priority_encoder_3 (
    .in0(InSel10), .out(priority_encoder_3_out));  // open: in1, gs, en_out, en_in
  Priority_Encoder #(.select_enc(1)) priority_encoder_4 (
    .in0(InSel11), .out(priority_encoder_4_out));  // open: in1, gs, en_out, en_in
  and and_14 (and_14_out, and_3_out, comparator_18_gt);
  and and_15 (and_15_out, and_3_out, comparator_18_eq);
  and and_16 (and_16_out, and_3_out, comparator_18_lt);
  and and_17 (and_17_out, O32, R1);
  and and_18 (and_18_out, I1, O32);
  and and_19 (and_19_out, I2, O32);
  and and_20 (and_20_out, S, O32);
  Adder #(.width(6)) adder_1 (.a(6'b100000), .b(bit_extender_1_out), .out(InsLabel8));  // open: cin, cout
  assign bit_extender_1_out = {{5{1'b0}}, priority_encoder_1_out};  // Bit_Extender bit_extender_1
  assign bit_extender_2_out = {{5{1'b0}}, priority_encoder_2_out};  // Bit_Extender bit_extender_2
  assign bit_extender_3_out = {{5{1'b0}}, priority_encoder_3_out};  // Bit_Extender bit_extender_3
  assign bit_extender_4_out = {{5{1'b0}}, priority_encoder_4_out};  // Bit_Extender bit_extender_4
  and and_21 (and_21_out, O33, R1);
  Adder #(.width(6)) adder_2 (.a(6'b100001), .b(bit_extender_2_out), .out(InsLabel9));  // open: cin, cout
  Adder #(.width(6)) adder_3 (.a(6'b100010), .b(bit_extender_3_out), .out(InsLabel10));  // open: cin, cout
  Adder #(.width(6)) adder_4 (.a(6'b100011), .b(bit_extender_4_out), .out(InsLabel11));  // open: cin, cout
  Priority_Encoder #(.select_enc(2)) priority_encoder_5 (
    .in0(and_14_out), .in1(and_15_out), .in2(and_16_out), .out(priority_encoder_5_out));  // open: in3, gs, en_out, en_in
  and and_22 (and_22_out, and_27_out, comparator_20_gt);
  and and_23 (and_23_out, comparator_20_lt, and_27_out);
  and and_24 (and_24_out, O34, R1);
  and and_25 (and_25_out, I2, O34);
  and and_26 (and_26_out, B, O34);
  Adder #(.width(6)) adder_5 (.a({6{1'b0}}), .b(bit_extender_5_out), .out(InsLabel1));  // open: cin, cout
  assign bit_extender_5_out = {{4{1'b0}}, priority_encoder_5_out};  // Bit_Extender bit_extender_5
  Comparator #(.mode("unsigned"), .width(7)) comparator_20 (
    .a(7'b0000001), .b(Instruction[31:25]), .gt(comparator_20_gt), .lt(comparator_20_lt));  // open: eq
  and and_27 (and_27_out, O35, R1);
  and and_28 (and_28_out, I2, O35);
  and and_29 (and_29_out, B, O35);
  Priority_Encoder #(.select_enc(4)) priority_encoder_6 (
    .in0(and_1_out), .in1(and_2_out), .in2(and_21_out), .in3(and_17_out), .in4(and_24_out), .in5(and_22_out),
    .in6(and_23_out), .in7(and_30_out), .in8(and_33_out), .out(priority_encoder_6_out));  // open: in9, in10, in11, in12, in13, in14, in15, gs, en_out, en_in
  and and_30 (and_30_out, O36, R1);
  and and_31 (and_31_out, I2, O36);
  and and_32 (and_32_out, B, O36);
  or or_1 (InSel1, and_14_out, and_15_out, and_16_out);
  assign bit_extender_6_out = {{2{1'b0}}, priority_encoder_6_out};  // Bit_Extender bit_extender_6
  and and_33 (and_33_out, O37, R1);
  and and_34 (and_34_out, I2, O37);
  and and_35 (and_35_out, B, O37);
  or or_2 (InSel2, and_1_out, and_2_out, and_21_out, and_17_out, and_24_out, and_22_out, and_23_out, and_30_out, and_33_out);
  Adder #(.width(6)) adder_6 (.a(bit_extender_6_out), .b(6'b000011), .out(InsLabel2));  // open: cin, cout
  or or_3 (InSel5, and_20_out, and_12_out, and_6_out);
  or or_4 (InSel7, and_7_out, and_13_out, and_26_out, and_29_out, and_32_out, and_35_out);
  Priority_Encoder priority_encoder_7 (
    .in0(and_7_out), .in1(and_13_out), .in2(and_26_out), .in3(and_29_out), .in4(and_32_out),
    .in5(and_35_out), .out(priority_encoder_7_out));  // open: in6, in7, en_in, gs, en_out
  or or_5 (InSel3, and_4_out, and_10_out, and_18_out);
  Priority_Encoder #(.select_enc(2)) priority_encoder_8 (
    .in0(and_4_out), .in1(and_10_out), .in2(and_18_out), .out(priority_encoder_8_out));  // open: in3, gs, en_out, en_in
  Priority_Encoder #(.select_enc(2)) priority_encoder_9 (
    .in0(and_6_out), .in1(and_12_out), .in2(and_20_out), .out(priority_encoder_9_out));  // open: in3, gs, en_out, en_in
  assign bit_extender_7_out = {{3{1'b0}}, priority_encoder_7_out};  // Bit_Extender bit_extender_7
  // Probe on bit_extender_7_out
  not not_1 (not_1_out, BrLt);
  assign bit_extender_8_out = {{4{1'b0}}, priority_encoder_8_out};  // Bit_Extender bit_extender_8
  assign bit_extender_9_out = {{4{1'b0}}, priority_encoder_9_out};  // Bit_Extender bit_extender_9
  // Probe on InsLabel7
  Adder #(.width(6)) adder_7 (.a(6'b011010), .b(bit_extender_7_out), .out(InsLabel7));  // open: cin, cout
  not not_2 (not_2_out, BrEq);
  not not_3 (not_3_out, BrLt);
  Adder #(.width(6)) adder_8 (.a(6'b001100), .b(bit_extender_8_out), .out(InsLabel3));  // open: cin, cout
  Adder #(.width(6)) adder_9 (.a(6'b010111), .b(bit_extender_9_out), .out(InsLabel5));  // open: cin, cout
  and and_36 (and_36_out, and_29_out, not_1_out);
  and and_37 (and_37_out, and_32_out, BrLt);
  and and_38 (and_38_out, and_7_out, BrEq);
  and and_39 (and_39_out, and_13_out, not_2_out);
  and and_40 (and_40_out, and_26_out, BrLt);
  and and_41 (and_41_out, and_35_out, not_3_out);
  Priority_Encoder #(.select_enc(4)) priority_encoder_10 (
    .in0(and_5_out), .in1(and_11_out), .in2(and_19_out), .in3(and_25_out), .in6(and_31_out),
    .in7(and_34_out), .out(priority_encoder_10_out));  // open: in4, in5, in8, in9, in10, in11, in12, in13, in14, in15, gs, en_out, en_in
  Comparator #(.mode("unsigned"), .width(7)) comparator_21 (
    .a(7'b0000001), .b(Instruction[31:25]), .gt(comparator_21_gt), .lt(comparator_21_lt));  // open: eq
  or or_6 (InSel4, and_5_out, and_11_out, and_19_out, and_25_out, and_31_out, and_34_out);
  and and_42 (and_42_out, and_28_out, comparator_21_gt);
  and and_43 (and_43_out, and_28_out, comparator_21_lt);
  Priority_Encoder #(.select_enc(4)) priority_encoder_11 (
    .in0(InSel1), .in1(InSel2), .in2(InSel3), .in3(InSel4), .in4(InSel5), .in5(InSel6), .in6(InSel7),
    .in7(InSel8), .in8(InSel9), .in9(InSel10), .in10(InSel11), .out(priority_encoder_11_out));  // open: in11, in12, in13, in14, in15, gs, en_out, en_in
  assign bit_extender_10_out = {{2{1'b0}}, priority_encoder_10_out};  // Bit_Extender bit_extender_10
  Adder #(.width(6)) adder_10 (.a(bit_extender_10_out), .b(6'b001111), .out(InsLabel4));  // open: cin, cout
  Priority_Encoder #(.select_enc(2)) priority_encoder_12 (
    .in0(and_42_out), .in1(and_43_out), .out(priority_encoder_12_out));  // open: in2, in3, gs, en_out, en_in
  or or_7 (InSel6, and_42_out, and_43_out);
  Multiplexer #(.select(4)) multiplexer_1 (
    .in0(1'b0), .in1(and_38_out), .in2(and_39_out), .in4(and_37_out), .in5(and_36_out), .in6(and_41_out),
    .in7(and_40_out), .in9(InSel10), .in10(InSel11), .out(PCSel), .sel(priority_encoder_13_out));  // open: in3, in8, in11, in12, in13, in14, in15
  Priority_Encoder #(.select_enc(4)) priority_encoder_13 (
    .in0(1'b1), .in1(and_38_out), .in2(and_39_out), .in4(and_37_out), .in5(and_36_out), .in6(and_41_out),
    .in7(and_40_out), .in9(InSel10), .in10(InSel11), .out(priority_encoder_13_out));  // open: in3, in8, in11, in12, in13, in14, in15, gs, en_out, en_in
  Adder #(.width(6)) adder_11 (.a(6'b010011), .b(bit_extender_11_out), .out(InsLabel6));  // open: cin, cout
  assign bit_extender_11_out = {{4{1'b0}}, priority_encoder_12_out};  // Bit_Extender bit_extender_11
  Multiplexer #(.select(4), .width(6)) multiplexer_2 (
    .in0(InsLabel1), .in1(InsLabel2), .in2(InsLabel3), .in3(InsLabel4), .in4(InsLabel5), .in5(InsLabel6),
    .in6(InsLabel7), .in7(InsLabel8), .in8(InsLabel9), .in9(InsLabel10), .in10(InsLabel11), .out(InsLabel),
    .sel(priority_encoder_11_out));  // open: in11, in12, in13, in14, in15

  // Other names for the same wires on the sheet: funct7[6:0] = Instruction[31:25]; J1 = InSel10; U1 = InSel8;
  //   U2 = InSel9

  // Notes on the sheet:
  //   INPUTS to your circuit
  //   Connect ROM Input here ->
  //   contents of rom_1 (hex, n*v repeats v):
  //   1001 1401 1601 1081 1481 1581 1101 1201 1281 1681 1301 1381 41 41 41 1041 10c1 1141 1241 12c1 16c1
  //   1341 13c1 842 842 842 4*64 74 74 1067 17c7 2069 2041
  //   R typ inst opcode
  //   I type inst opcodes
  //   S type opcodes
  //   B type opcodes
  //   U type opcodes
  //   J type opcodes
  //   I type(jalr) opcode
  //   ROM FOR CONTROL LOGIC
  //   DON'T CHANGE THE LOCATIONS OF THE INPUTS AND OUTPUTS!
  //   This is only if you choose to do the ROM option
  //   CONNECT
  //   WIRE
  //   TO
  //   USE
  //   ROM
  //   OUTPUT from your circuit
  //   Reminder: If using ROM, use combinational logic for PCSel
  //   this one needs 2
  //   beq
  //   bne
  //   blt
  //   bge
  //   bltu
  //   bgeu
endmodule
